// Logisim project rpl.circ as structural Verilog: 1 circuit, main circuit RPL
module RPL (
  input  CLK,
  input  CLR,
  input  [15:0] in_3,
  input  [15:0] in_4,
  output [7:0] out_5,
  output [7:0] out_6,
  output PreLoading,
  output [7:0] out_8,
  output [7:0] out_9,
  output [15:0] out_10
);

  wire comparator_1_lt, RPL_HASDATA_data;
  wire [15:0] counter_1_q;

  Counter #(.width(16), .max('hffff)) counter_1 (
    .count(PreLoading), .Q(counter_1_q), .clk(CLK), .clr(CLR));  // open: load, D, carry, preset, down
  Adder #(.width(16)) adder_1 (.a(counter_1_q), .b(in_3), .out(out_10));  // open: cin, cout
  Comparator #(.width(16), .mode("unsigned")) comparator_1 (
    .a(out_10), .b(in_4), .lt(comparator_1_lt));  // open: gt, eq
  ROM #(.addrWidth(2), .dataWidth(1), .Select("low")) RPL_HASDATA (.addr(2'b00), .data(RPL_HASDATA_data));
  and and_1 (PreLoading, comparator_1_lt, RPL_HASDATA_data);
  ROM #(.addrWidth(16), .Select("low")) RPL_RAM3 (.addr(out_10), .data(out_5));
  ROM #(.addrWidth(16), .Select("low")) RPL_RAM2 (.addr(out_10), .data(out_6));
  ROM #(.addrWidth(16), .Select("low")) RPL_RAM1 (.addr(out_10), .data(out_8));
  ROM #(.addrWidth(16), .Select("low")) RPL_RAM0 (.addr(out_10), .data(out_9));

  // Other names for the same wires on the sheet: ADDR[15:0] = out_10; END[15:0] = in_4; RAM0[7:0] = out_9;
  //   RAM1[7:0] = out_8; RAM2[7:0] = out_6; RAM3[7:0] = out_5; START[15:0] = in_3

  // Notes on the sheet:
  //   contents of RPL_RAM3 (hex, n*v repeats v):
  //   2048*0 DE DE DE DE DE DE DE DE DE DE 00 00
  //   contents of RPL_RAM2 (hex, n*v repeats v):
  //   2048*0 AD AD AD AD AD AD AD AD AD AD 00 00
  //   contents of RPL_RAM1 (hex, n*v repeats v):
  //   2048*0 BE BE BE BE BE BE BE BE BE BE 00 00
  //   contents of RPL_RAM0 (hex, n*v repeats v):
  //   2048*0 EF EF EF EF EF EF EF EF EF EF 00 00
endmodule
